# Fritzing sketch Laser Brain Wiring (saved by Fritzing 0.9.3b)
circuit board: 8.46667cm x 5.64444cm
breadboards: 1

parts:
  C3-1 = Ceramic Capacitor [capacitance=1µF voltage=35V package="100 mil [THT, multilayer]"]
  C2-1 = Ceramic Capacitor [capacitance=1µF voltage=35V package="100 mil [THT, multilayer]"]
  C4-1 = Ceramic Capacitor [capacitance=1µF voltage=35V package="100 mil [THT, multilayer]"]
  C1-1 = Ceramic Capacitor [capacitance=1µF voltage=35V package="100 mil [THT, multilayer]"]
  Serial_1_&_2 = RS232 Transceiver [package=dil16]
  Serial_3_&_4 = RS232 Transceiver [package=dil16]
  C1-2 = Ceramic Capacitor [capacitance=1µF voltage=35V package="100 mil [THT, multilayer]"]
  C2-2 = Ceramic Capacitor [capacitance=1µF voltage=35V package="100 mil [THT, multilayer]"]
  C3-2 = Ceramic Capacitor [capacitance=1µF voltage=35V package="100 mil [THT, multilayer]"]
  C4-2 = Ceramic Capacitor [capacitance=1µF voltage=35V package="100 mil [THT, multilayer]"]
  Laser_Triggering = BNC [package=bnc]
  GPIO_BNC1 = BNC [package=bnc]
  GPIO_BNC2 = BNC [package=bnc]
  GPIO_BNC3 = BNC [package=bnc]
  GPIO_BNC4 = BNC [package=bnc]
  Power = Round Pushbutton
  Serial_3 = DB9 Connector For Basic Serial [package=db9]
  Serial_1 = DB9 Connector For Basic Serial [package=db9]
  Serial_2 = DB9 Connector For Basic Serial [package=db9]
  Pump_Cap = Ceramic Capacitor [capacitance=1µF voltage=35V package="100 mil [THT, multilayer]"]
  Cancel_Dep = Round Pushbutton
  LLC1 = I2C level shifter bidirectional
  GPIO1_HV = DB9 Connector [package=db9]
  BeagleBone1 = BeagleBone Black - Labeled Pinout
  GPIO2_LV = DB9 Connector [package=db9]

nets (from the schematic view):
  N1: C3-1.0, Serial_1_&_2.V+
  GND: C3-1.1, C4-1.1, Serial_1_&_2.GND, Serial_3_&_4.GND, C3-2.1, C4-2.1, Laser_Triggering.GND, GPIO_BNC1.GND, GPIO_BNC2.GND, GPIO_BNC3.GND, GPIO_BNC4.GND, Power.leg1, Serial_3.5, Serial_1.5, Serial_2.5, Pump_Cap.0, LLC1.GND, GPIO1_HV.5, GPIO1_HV.6, BeagleBone1.P9_1, BeagleBone1.P9_2, BeagleBone1.P9_43, BeagleBone1.P9_44, BeagleBone1.P9_45, BeagleBone1.P9_46, BeagleBone1.P8_2, GPIO2_LV.5, GPIO2_LV.6
  N2: C2-1.0, Serial_1_&_2.C2-
  N3: C2-1.1, Serial_1_&_2.C2+
  N4: C4-1.0, Serial_1_&_2.V-
  N5: C1-1.0, Serial_1_&_2.C1-
  N6: C1-1.1, Serial_1_&_2.C1+
  N7: Serial_1_&_2.T2OUT, Serial_2.3
  N8: Serial_1_&_2.R2IN, Serial_2.2
  N9: Serial_1_&_2.R2OUT, BeagleBone1.P9_22
  N10: Serial_1_&_2.T2IN, BeagleBone1.P9_21
  N11: Serial_1_&_2.T1IN, BeagleBone1.P9_24
  N12: Serial_1_&_2.R1OUT, BeagleBone1.P9_26
  N13: Serial_1_&_2.R1IN, Serial_1.2
  N14: Serial_1_&_2.T1OUT, Serial_1.3
  5V: Serial_1_&_2.VCC, Serial_3_&_4.VCC, Pump_Cap.1, LLC1.HV, BeagleBone1.P9_7
  N15: Serial_3_&_4.C1+, C1-2.1
  N16: Serial_3_&_4.V+, C3-2.0
  N17: Serial_3_&_4.C1-, C1-2.0
  N18: Serial_3_&_4.C2+, C2-2.1
  N19: Serial_3_&_4.C2-, C2-2.0
  N20: Serial_3_&_4.V-, C4-2.0
  N21: Serial_3_&_4.R2OUT, BeagleBone1.P9_11
  N22: Serial_3_&_4.T2IN, BeagleBone1.P9_13
  N23: Serial_3_&_4.R1IN, Serial_3.2
  N24: Serial_3_&_4.T1OUT, Serial_3.3
  N25: Laser_Triggering.OUT, BeagleBone1.P8_17
  N26: GPIO_BNC1.OUT, BeagleBone1.P8_16
  N27: GPIO_BNC2.OUT, BeagleBone1.P8_15
  N28: GPIO_BNC3.OUT, BeagleBone1.P8_18
  N29: GPIO_BNC4.OUT, BeagleBone1.P8_26
  N30: Power.leg0, BeagleBone1.P9_9
  N31: Cancel_Dep.leg0, BeagleBone1.P9_15
  3.3V: Cancel_Dep.leg1, LLC1.LV, BeagleBone1.P9_3, BeagleBone1.P9_4
  N32: LLC1.LV4, BeagleBone1.P9_25
  N33: LLC1.LV3, BeagleBone1.P9_29
  N34: LLC1.LV2, BeagleBone1.P9_28
  N35: LLC1.LV1, BeagleBone1.P9_27
  N36: LLC1.HV1, GPIO1_HV.1
  N37: LLC1.HV2, GPIO1_HV.2
  N38: LLC1.HV3, GPIO1_HV.3
  N39: LLC1.HV4, GPIO1_HV.4
  N40: GPIO1_HV.7, BeagleBone1.P9_17
  N41: GPIO1_HV.8, BeagleBone1.P9_41
  N42: GPIO1_HV.9, BeagleBone1.P9_19
  N43: BeagleBone1.P8_7, GPIO2_LV.1
  N44: BeagleBone1.P8_8, GPIO2_LV.2
  N45: BeagleBone1.P8_9, GPIO2_LV.3
  N46: BeagleBone1.P8_10, GPIO2_LV.4
  N47: BeagleBone1.P8_11, GPIO2_LV.7
  N48: BeagleBone1.P8_12, GPIO2_LV.8
  N49: BeagleBone1.P8_14, GPIO2_LV.9

notes:
  Notes:
  * Red/White Banded wires are red within the actual box
  this distinciton is to show which wires carry voltage vs
  GPIO
  * Green wires were used for serial connections
  * I took liberties with ground routing in this drawing (e.g.
  the BNC jacks are not daisy chained)
  * Anything not on the breadboard is connected to the
  outside panels of the box.
  * Wiring to the GPIO DB9s is not direct as depicted here,
  there is a wire from the BBB to the breadboard then
  then a soldered wire to the DB9
  * The Schematic is more useful for seeing connections
  clearly.
  Pin: Wired To: Cond. Color:
  GPIO1_HV1: Sub STEP Yellow
  GPIO1_HV2: Sub DIR Purple
  GPIO1_HV3: Targ STEP Orange
  GPIO1_HV4: Targ DIR Green
  GPIO1_HV5: GROUND Black
  GPIO1_HV6: GROUND Blue
  GPIO1_HV7: N/A White
  GPIO1_HV8: N/A Grey
  GPIO1_HV9: N/A Red
  Pin: Wired To:
  GPIO1_LV1: SubTop Switch
  GPIO2_LV2: SubTop Switch
  GPIO3_LV3: N/A
  GPIO4_LV4: N/A
  GPIO5_LV5: GROUND
  GPIO6_LV6: GROUND
  GPIO7_LV7: N/A
  GPIO8_LV8: N/A
  GPIO9_LV9: N/A

custom parts:
  DB9 Connector For Basic Serial: DB9 Connector Standard DB9 (D-Sub 9) serial connector. Can be used for CAN bus as well as RS485 and RS232. Footprint production proven. Spark Fun Electronics SKU : PRT-00429
  DB9 Connector: DB9 Connector Standard DB9 (D-Sub 9) serial connector. Can be used for CAN bus as well as RS485 and RS232. Footprint production proven. Spark Fun Electronics SKU : PRT-00429
  BeagleBone Black - Labeled Pinout: BeagleBone Black rev. A5B
