# Fritzing sketch RPi Laser Brain (saved by Fritzing 0.9.3b)
breadboards: 1

parts:
  RPi = Raspberry Pi 3 [part_number=RPI-3-V1.2]
  PermaProto_HAT = Adafruit Perma-Proto HAT [part_number="Adafruit #2314"]
  MAX232-1 = RS232 Transceiver [package=dil16]
  MAX232-2 = RS232 Transceiver [package=dil16]
  LLC = I2C level shifter bidirectional
  C1-1 = Ceramic Capacitor [capacitance=1µF voltage=35V package="100 mil [THT, multilayer]"]
  C2-1 = Ceramic Capacitor [capacitance=1µF voltage=35V package="100 mil [THT, multilayer]"]
  C(V+)-1 = Ceramic Capacitor [capacitance=1µF voltage=35V package="100 mil [THT, multilayer]"]
  C(V-)-1 = Ceramic Capacitor [capacitance=1µF voltage=35V package="100 mil [THT, multilayer]"]
  C(V-)-2 = Ceramic Capacitor [capacitance=1µF voltage=35V package="100 mil [THT, multilayer]"]
  C1-2 = Ceramic Capacitor [capacitance=1µF voltage=35V package="100 mil [THT, multilayer]"]
  C(V+)-2 = Ceramic Capacitor [capacitance=1µF voltage=35V package="100 mil [THT, multilayer]"]
  C2-2 = Ceramic Capacitor [capacitance=1µF voltage=35V package="100 mil [THT, multilayer]"]
  Serial1 = DB9 Connector For Basic Serial [package=db9]
  GPIO_HV = DB9 Connector [package=db9]
  BNC1 = BNC [package=bnc]
  BNC5 = BNC [package=bnc]
  BNC4 = BNC [package=bnc]
  BNC2_-_Laser_Out = BNC [package=bnc]
  BNC3 = BNC [package=bnc]
  Serial2 = DB9 Connector For Basic Serial [package=db9]
  Serial3 = DB9 Connector For Basic Serial [package=db9]
  GPIO_LV = DB9 Connector [package=db9]
  Power = Round Pushbutton
  Aux = Round Pushbutton
  Arduino = Arduino Nano (Rev3.0)
  R1 = Resistor [tolerance=±5% resistance=10k package=THT]

nets:
  3.3V: RPi.3v3, RPi.3V3, PermaProto_HAT.3.3V, PermaProto_HAT.N$42, LLC.LV
  N1: RPi.GPIO2, PermaProto_HAT.SDA
  N2: RPi.GPIO3, PermaProto_HAT.SCL, Power.leg0
  N3: RPi.GIPO4, PermaProto_HAT.GPIO4
  GND: RPi.GND, PermaProto_HAT.GND, PermaProto_HAT.N$20, PermaProto_HAT.N$43, PermaProto_HAT.N$54, PermaProto_HAT.N$61, MAX232-1.GND, MAX232-2.GND, LLC.GND, C(V+)-1.0, C(V-)-1.0, C(V-)-2.0, C(V+)-2.0, Serial1.5, GPIO_HV.5, BNC1.GND, BNC5.GND, BNC4.GND, BNC2_-_Laser_Out.GND, BNC3.GND, Serial2.5, Serial3.5, GPIO_LV.5, Power.leg1, Aux.leg1, Arduino.GND
  N4: RPi.GIPO17, PermaProto_HAT.GPIO17, Aux.leg0
  N5: RPi.GIPO27, PermaProto_HAT.GPIO27, GPIO_LV.2
  N6: RPi.GIPO22, PermaProto_HAT.GPIO22, GPIO_LV.3
  N7: RPi.GIPO10, PermaProto_HAT.SPI_MOSI
  N8: RPi.GIPO9, PermaProto_HAT.SPI_MISO, PermaProto_HAT.N$49, MAX232-2.R1OUT
  N9: RPi.GIPO11, PermaProto_HAT.SPI_SCLK
  N10: RPi.ID_SD, PermaProto_HAT.EEDATA
  N11: RPi.GIPO5, PermaProto_HAT.GPIO5, GPIO_LV.8
  N12: RPi.GIPO6, PermaProto_HAT.GPIO6, GPIO_LV.9
  N13: RPi.GIPO13, PermaProto_HAT.GPIO13, PermaProto_HAT.N$58, MAX232-1.R1OUT
  N14: RPi.GIPO19, PermaProto_HAT.GPIO19, PermaProto_HAT.N$44, LLC.LV3
  N15: RPi.GIPO26, PermaProto_HAT.GPIO26
  N16: RPi.GIPO21, PermaProto_HAT.GPIO21, PermaProto_HAT.N$39, LLC.LV1
  N17: RPi.GIPO20, PermaProto_HAT.GPIO20, PermaProto_HAT.N$41, LLC.LV2
  N18: RPi.GIPO16, PermaProto_HAT.GPIO16, PermaProto_HAT.N$45, LLC.LV4
  N19: RPi.GIPO12, PermaProto_HAT.GPIO12, PermaProto_HAT.N$57, MAX232-1.T1IN
  N20: RPi.ID_SC, PermaProto_HAT.EECLK
  N21: RPi.GIPO7, PermaProto_HAT.SPI_CE1
  N22: RPi.GIPO8, PermaProto_HAT.SPI_CE0, PermaProto_HAT.N$50, MAX232-2.T1IN
  N23: RPi.GIPO25, PermaProto_HAT.GPIO25, GPIO_LV.7
  N24: RPi.GIPO24, PermaProto_HAT.GPIO24, GPIO_LV.6
  N25: RPi.GIPO23, PermaProto_HAT.GPIO23, GPIO_LV.4
  N26: RPi.GIPO18, PermaProto_HAT.GPIO18, GPIO_LV.1
  N27: RPi.GIPO15, PermaProto_HAT.RXD, PermaProto_HAT.N$55, MAX232-1.R2OUT
  N28: RPi.GIPO14, PermaProto_HAT.TXD, PermaProto_HAT.N$56, MAX232-1.T2IN
  5V: RPi.5V, PermaProto_HAT.5.0V, PermaProto_HAT.N$22, PermaProto_HAT.N$53, PermaProto_HAT.N$62, MAX232-1.VCC, MAX232-2.VCC, LLC.HV
  N29: PermaProto_HAT.N$1, MAX232-1.C1+, C1-1.1
  N30: PermaProto_HAT.N$2, MAX232-1.V+, C(V+)-1.1
  N31: PermaProto_HAT.N$3, MAX232-1.C1-, C1-1.0
  N32: PermaProto_HAT.N$4, MAX232-1.C2+, C2-1.1
  N33: PermaProto_HAT.N$5, MAX232-1.C2-, C2-1.0
  N34: PermaProto_HAT.N$6, MAX232-1.V-, C(V-)-1.1
  N35: PermaProto_HAT.N$7, MAX232-1.R2IN, Serial1.2
  N36: PermaProto_HAT.N$8, MAX232-1.T2OUT, Serial1.3
  N37: PermaProto_HAT.N$9, MAX232-2.C1+, C1-2.1
  N38: PermaProto_HAT.N$10, MAX232-2.V+, C(V+)-2.1
  N39: PermaProto_HAT.N$11, MAX232-2.C1-, C1-2.0
  N40: PermaProto_HAT.N$12, MAX232-2.C2+, C2-2.1
  N41: PermaProto_HAT.N$13, MAX232-2.C2-, C2-2.0
  N42: PermaProto_HAT.N$14, MAX232-2.V-, C(V-)-2.1
  N43: PermaProto_HAT.N$15, MAX232-2.T2OUT
  N44: PermaProto_HAT.N$17, LLC.HV4, Arduino.RESET, R1.Pin_0
  N45: PermaProto_HAT.N$19, LLC.HV3, Arduino.A6
  N46: PermaProto_HAT.N$21, LLC.HV2, Arduino.A5
  N47: PermaProto_HAT.N$23, LLC.HV1, Arduino.A4
  N48: PermaProto_HAT.N$47, MAX232-2.R2OUT
  N49: PermaProto_HAT.N$48, MAX232-2.T2IN
  N50: PermaProto_HAT.N$51, MAX232-2.R1IN, Serial3.2
  N51: PermaProto_HAT.N$52, MAX232-2.T1OUT, Serial3.3
  N52: PermaProto_HAT.N$59, MAX232-1.T1OUT, Serial2.3
  N53: PermaProto_HAT.N$60, MAX232-1.R1IN, Serial2.2
  N54: GPIO_HV.1, Arduino.D2
  N55: GPIO_HV.2, Arduino.D3
  N56: GPIO_HV.3, Arduino.D4
  N57: GPIO_HV.4, Arduino.D5
  N58: GPIO_HV.6, Arduino.D6
  N59: GPIO_HV.7, Arduino.D7
  N60: GPIO_HV.8, Arduino.D8
  N61: GPIO_HV.9, Arduino.D9
  N62: BNC1.OUT, Arduino.D12/MISO
  N63: BNC5.OUT, Arduino.A3
  N64: BNC4.OUT, Arduino.A2
  N65: BNC2_-_Laser_Out.OUT, Arduino.D11/MOSI
  N66: BNC3.OUT, Arduino.D10
  N67: Arduino.5V, R1.Pin_1

notes:
  :Pi Serial: :External: :MAX232:
  RX0/TX0 Serial 1 1-Chan2
  RX5/TX5 Serial 2 1-Chan1
  RX4/TX4 Serial 3 2-Chan1
  Notes:
  * Green wires were used for serial connections
  * I took liberties with ground routing in this drawing (e.g.
  the BNC jacks are not daisy chained)
  * Anything not on the breadboard is connected to the
  outside panels of the box.
  * Wiring to GPIO_LV is not direct as depicted here,
  there is a wire from the BBB to the breadboard then
  then a soldered wire to the DB9
  * The Schematic is more useful for seeing connections
  clearly.
  *Actual hardware is a Raspberry Pi 4 and an Arduino Nano Every, but I couldn't find Fritzing parts for those items. However the parts used in this diagram should be slot in (pin-to-pin compatible) replacements
  * Dotted lines are due to missing connections in the HAT part
  Pin: Wired To: Cond. Color: GPIO#:
  GPIO1_LV1: SubTop Green 18
  GPIO2_LV2: N/A White 27
  GPIO3_LV3: SubBottom Red 22
  GPIO4_LV4: SubLimitHi Black 23
  GPIO5_LV5: GROUND Brown2 GND
  GPIO6_LV6: N/A White2 24
  GPIO7_LV7: N/A Green2 25
  GPIO8_LV8: N/A Red2 5
  GPIO9_LV9: N/A Black2 6
  Pin: Wired To: Cond. Color:
  GPIO1_HV1: Sub STEP Yellow
  GPIO1_HV2: Sub DIR Purple
  GPIO1_HV3: Targ STEP Orange
  GPIO1_HV4: Targ DIR Green
  GPIO1_HV5: GROUND Black
  GPIO1_HV6: GROUND Blue
  GPIO1_HV7: N/A White
  GPIO1_HV8: N/A Grey
  GPIO1_HV9: N/A Red
  Serial 2 = RPi uart5, TXD5 = GPIO12,
  RXD5 = GPIO13
  Serial 1 = RPi uart0, TXD5 = GPIO14,
  RXD0 = GPIO15
  Serial 3 = RPi uart4, TXD4 = GPIO08,
  RXD4 = GPIO09
  Cross Board GPIO:
  RPi Pin: Dir: Ard Pin: Function:
  21 <- A4 Sub Running
  20 <- A5 Targs Running
  19 <- A6 Laser Running
  16 -> RST Remote Reset

custom parts:
  Adafruit Perma-Proto HAT: To kick off the Adafruit HAT party, we have this Perma-Proto inspired plug in daughter board. It has a grid of 0.1" prototyping soldering holes for attaching chips, resistors, LED, potentiometers and more. The holes are connected underneath with traces to mimic the solderless breadboards you're familiar. There's also long power strips for +3V, +5V and Ground connections to the Pi. Near the top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
  DB9 Connector For Basic Serial: DB9 Connector Standard DB9 (D-Sub 9) serial connector. Can be used for CAN bus as well as RS485 and RS232. Footprint production proven. Spark Fun Electronics SKU : PRT-00429
  DB9 Connector: DB9 Connector Standard DB9 (D-Sub 9) serial connector. Can be used for CAN bus as well as RS485 and RS232. Footprint production proven. Spark Fun Electronics SKU : PRT-00429
  BNC: BNC Connector, Mouser Part# 5227161
